# Fritzing sketch P08_01_00-ANA608VarResist (saved by Fritzing 0.9.3b)
breadboards: 1

parts:
  ANA608 = female pin header, 4 pins [form="♀ (female)"]
  Capacitor = Electrolytic Capacitor [capacitance=1µF package="100 mil [THT, electrolytic]"]
  Solar_Cell = Photocell (LDR) [package=THT]
  R2 = Rotary Potentiometer (Small) [maximum_resistance=100kΩ package=THT]
  Inductor = Inductor [package="400 mil [THT]"]
  LED1 = LED - 5mm [color="Red (633nm)" package="5 mm [THT]"]

nets:
  N1: ANA608.pin1, Capacitor.-, Solar_Cell.pin_0, R2.leg2, LED1.cathode
  N2: ANA608.pin2, R2.wiper
  N3: ANA608.pin3, Inductor.pin_0, LED1.anode
  N4: ANA608.pin4, Capacitor.+, Solar_Cell.pin_1, Inductor.pin_1
