# Fritzing sketch P08_01_00-Main (saved by Fritzing 0.9.3b)
breadboards: 1

parts:
  U3 = attiny85 [package=dip]
  R1 = PHOTOCELL [package=photocell-kit]
  J1 = female pin header, 4 pins [form="♀ (female)"]
  R2 = Photocell (LDR) [package=THT]
  L1 = Inductor [package="400 mil [THT]"]
  D1 = Schottky Diode [part_number=1N5817 package="300 mil [THT]"]
  C1 = Electrolytic Capacitor [capacitance=1µF package="100 mil [THT, electrolytic]"]
  D2 = Rectifier Diode [part_number=1N4001 package="300 mil [THT]"]
  LED1 = LED - 5mm [color="Red (633nm)" package="5 mm [THT]"]
  LED2 = LED - 5mm [color="Green (565nm)" package="5 mm [THT]"]
  R3 = Resistor [tolerance=±5% resistance=10k package=THT]
  R4 = Resistor [tolerance=±5% resistance=10k package=THT]
  Part1 = Soil Moisture Sensor
  U4 = POT [package=alps_pot]
  BAT1 = Battery Holders [package=battery-aa]
  R5 = Resistor [tolerance=±5% resistance=470 package=THT]

nets:
  N1: U3.Pin_2, R3.Pin_0, Part1.SIG
  N2: U3.Pin_3, R4.Pin_0, U4.S
  N3: U3.Pin_4, R1.P$1, J1.pin1, C1.-, R3.Pin_1, R4.Pin_1, BAT1.-, R5.Pin_0
  N4: U3.Pin_5, LED1.cathode
  N5: U3.Pin_6, LED2.cathode
  N6: U3.Pin_7, Part1.VCC, U4.E
  N7: U3.Pin_8, D1.cathode, C1.+
  N8: R1.P$2, D2.anode
  N9: J1.pin2, R2.pin_1
  N10: J1.pin3, L1.pin_0, D1.anode
  N11: J1.pin4, R2.pin_0, L1.pin_1, D2.cathode, BAT1.+
  N12: LED1.anode, LED2.anode, R5.Pin_1
